# Fritzing sketch PCB-cnc (saved by Fritzing 1.0.1rc)
circuit board: 7.35842cm x 10.0802cm

parts:
  IR = fc-51 [package=THT]
  D1_mini_V4 = WeMos D1 Mini V4.0.0
  Piezo = Buzzer 12mm [package=buzzer-12mm-ns-kit]
  Servo_5V = Basic Servo  # not connected
  Servo_3_3v = Dagu DGServo 9g header (male) [package=THT]
  5v = female pin header, 2 pins [form="♀ (female)"]
  Switch_buzz = Round Pushbutton
  Interrupteur = SWITCH-MOMENTARY-2 [package=tactile-pth]
  Commutateur_12v_/_5v = Toggle Switch [package=THT]  # not connected
  5v_to_3_3 = AMS11176 module
  JP4 = Header 6 [package=molex-1x6_lock]
  R_202 = female pin header, 4 pins [form="♀ (female)"]
  Led = female pin header, 2 pins [form="♀ (female)"]

nets:
  N1: IR.pin1, D1_mini_V4.A0
  GND: IR.pin2, D1_mini_V4.GND, Piezo.2, Servo_3_3v.gnd, 5v.pin1, 5v_to_3_3.pin3, Led.pin1
  3.3V: IR.pin3, D1_mini_V4.3.3V, Servo_3_3v.Vcc, 5v_to_3_3.pin2, JP4.1
  N2: D1_mini_V4.0, Switch_buzz.leg0
  N3: D1_mini_V4.4/SDA, Servo_3_3v.pulse
  N4: D1_mini_V4.5/SCL, R_202.pin4
  N5: Piezo.1, Switch_buzz.leg1
  N6: 5v.pin2, Interrupteur.1
  N7: Interrupteur.2, 5v_to_3_3.pin1
  N8: R_202.pin1, Led.pin2

custom parts:
  WeMos D1 Mini V4.0.0: The D1 mini is a mini wifi board based on ESP-8266EX.
  AMS11176 module: DC-DC step-down modules ( input DC 4.5～7V , output DC 3.3V ).
