# Fritzing sketch ESP-D1-mini-led-matrix-etc (saved by Fritzing 1.0.1rc)
circuit board: 5.06901cm x 10.7262cm

parts:
  WeMos_D1_Mini1 = WeMos D1 Mini
  LED1 = LED - 5mm [color="Red (633nm)" current=0.030A package="5 mm [THT]"]
  PIR = PIR sensor
  220Ω = Resistor [tolerance=±5% power=0.25W resistance=220 package=THT]
  5v = female pin header, 2 pins [form="♀ (female)"]
  5x5_led_matrix = female pin header, 4 pins [form="♀ (female)"]
  10kΩ = Resistor [tolerance=±5% power=0.25W resistance=10k package=THT]
  Pont = Resistor [tolerance=±5% power=0.25W resistance=0 package=THT]
  DHT1 = DHT22 Humidity and Temperature Sensor
  10kΩ1 = Resistor [tolerance=±5% power=0.25W resistance=10k package=THT]
  Photores1 = Photocell (LDR) [power=0.25W dark_resistance_@0.01lx=300kΩ light_resistance_@100lx=400Ω luminance=10lx package=THT]
  5x5_led_matrix1 = female pin header, 4 pins [form="♀ (female)"]  # not connected

nets:
  VDD: WeMos_D1_Mini1.5V, PIR.VDD, 5v.pin2, 5x5_led_matrix.pin3, 10kΩ.Pin_1, DHT1.VDD, Photores1.pin_1
  N1: WeMos_D1_Mini1.A0, 10kΩ1.Pin_0, Photores1.pin_0
  N2: WeMos_D1_Mini1.D2, 5x5_led_matrix.pin2
  N3: WeMos_D1_Mini1.D5, 10kΩ.Pin_0, DHT1.DATA
  N4: WeMos_D1_Mini1.D6, 220Ω.Pin_0
  N5: WeMos_D1_Mini1.D7, PIR.SIG
  N6: WeMos_D1_Mini1.G, LED1.cathode, PIR.GND, 5v.pin1, 5x5_led_matrix.pin4, Pont.Pin_0
  N7: LED1.anode, 220Ω.Pin_1
  N8: Pont.Pin_1, DHT1.GND, 10kΩ1.Pin_1
