# Fritzing sketch simple-test (saved by Fritzing 0.9.10b)
breadboards: 1

parts:
  U1 = ATTINY13 [package=dip]
  LED1 = LED - 3mm [color="Red (633nm)" current=0.030 package="3 mm [THT]"]
  R1 = Resistor [tolerance=±5% power=0.25 resistance=220 package=THT]

nets:
  N1: U1.PB5(NRES), U1.VCC
  N2: U1.PB3(ADC3), U1.PB2(SCK_ADC1)
  N3: U1.PB4(ADC2), U1.PB1(MISO)
  N4: U1.GND, U1.PB0(MOSI), LED1.anode
  N5: LED1.cathode, R1.Pin_0
